# Fritzing sketch Joystick (saved by Fritzing 0.9.3b)

parts:
  Bauteil1 = Arduino Uno (Rev3)
  Bauteil2 = Thumb Joystick

nets:
  N1: Bauteil1.A0, Bauteil2.HORZ
  N2: Bauteil1.A1, Bauteil2.VERT
  N3: Bauteil1.D2, Bauteil2.SEL
  5V: Bauteil1.5V, Bauteil2.VCC
  GND: Bauteil1.GND, Bauteil2.GND
